// Logisim project 8-Bit-Addierwerk.circ as structural Verilog: 4 circuits, main circuit main
module Halbaddierer (
  input  x,
  input  y,
  output C,
  output S
);

  and and_1 (C, x, y);
  xor xor_1 (S, x, y);
endmodule

module main (
  input  in_1,
  input  in_2,
  input  in_3,
  input  in_4,
  input  in_5,
  input  in_6,
  input  in_7,
  input  in_8,
  input  in_9,
  input  in_10,
  input  in_11,
  input  in_12,
  input  in_13,
  input  in_14,
  input  in_15,
  input  in_16
);

  wire [0:0] n8_bit_addierwerk_1_cout;
  wire [7:0] n8_bit_addierwerk_1_s;

  LED led_1 (.in(n8_bit_addierwerk_1_cout[0]));
  LED led_2 (.in(n8_bit_addierwerk_1_s[6]));
  LED led_3 (.in(n8_bit_addierwerk_1_s[7]));
  LED led_4 (.in(n8_bit_addierwerk_1_s[5]));
  _8_bit_Addierwerk u_8_bit_addierwerk_1 (
    .Cin(1'b0), .A({in_1, in_2, in_3, in_4, in_5, in_6, in_7, in_8}),
    .B({in_9, in_10, in_11, in_12, in_13, in_14, in_15, in_16}), .Cout(n8_bit_addierwerk_1_cout[0]),
    .S(n8_bit_addierwerk_1_s));
  LED led_5 (.in(n8_bit_addierwerk_1_s[4]));
  LED led_6 (.in(n8_bit_addierwerk_1_s[3]));
  LED led_7 (.in(n8_bit_addierwerk_1_s[2]));
  LED led_8 (.in(n8_bit_addierwerk_1_s[1]));
  LED led_9 (.in(n8_bit_addierwerk_1_s[0]));
  Hex_Digit_Display hex_digit_display_1 (.value({3'b000, n8_bit_addierwerk_1_cout[0]}));  // open: dp
  Hex_Digit_Display hex_digit_display_2 (.value({in_1, in_2, in_3, in_4}));  // open: dp
  Hex_Digit_Display hex_digit_display_3 (.value({in_5, in_6, in_7, in_8}));  // open: dp
  Hex_Digit_Display hex_digit_display_4 (.value({in_9, in_10, in_11, in_12}));  // open: dp
  Hex_Digit_Display hex_digit_display_5 (.value({in_13, in_14, in_15, in_16}));  // open: dp
  Hex_Digit_Display hex_digit_display_6 (.value(n8_bit_addierwerk_1_s[7:4]));  // open: dp
  Hex_Digit_Display hex_digit_display_7 (.value(n8_bit_addierwerk_1_s[3:0]));  // open: dp
  // Probe on {in_1, in_2, in_3, in_4, in_5, in_6, in_7, in_8}
  // Probe on {in_9, in_10, in_11, in_12, in_13, in_14, in_15, in_16}
  // Probe on {n8_bit_addierwerk_1_cout[0], n8_bit_addierwerk_1_s}

  // Notes on the sheet:
  //   +
  //   8-Bit Addierwerk
  //   Result:   2^8         2^7           2^6         2^5          2^4         2^3          2^2         2^1          2^0
  //   ALU
  //   v1:   2^7         2^6           2^5         2^4          2^3         2^2          2^1         2^0
  //   v2:   2^7         2^6           2^5         2^4          2^3         2^2          2^1         2^0
  //   +
  //   =
endmodule

module Volladdierer (
  input  x,
  input  y,
  input  Cin,
  output Cout,
  output S
);

  wire halbaddierer_1_c, halbaddierer_1_s, halbaddierer_2_c;

  Halbaddierer halbaddierer_1 (.x(x), .y(y), .C(halbaddierer_1_c), .S(halbaddierer_1_s));
  or or_1 (Cout, halbaddierer_1_c, halbaddierer_2_c);
  Halbaddierer halbaddierer_2 (.x(halbaddierer_1_s), .y(Cin), .C(halbaddierer_2_c), .S(S));
endmodule

module _8_bit_Addierwerk (
  input  Cin,
  input  [7:0] A,
  input  [7:0] B,
  output Cout,
  output [7:0] S
);

  wire volladdierer_1_cout, volladdierer_2_cout, volladdierer_3_cout, volladdierer_4_cout,
       volladdierer_5_cout, volladdierer_6_cout, volladdierer_7_cout;

  Volladdierer volladdierer_1 (.x(A[0]), .y(B[0]), .Cin(Cin), .Cout(volladdierer_1_cout), .S(S[0]));
  Volladdierer volladdierer_2 (.x(A[1]), .y(B[1]), .Cin(volladdierer_1_cout), .Cout(volladdierer_2_cout), .S(S[1]));
  Volladdierer volladdierer_3 (.x(A[2]), .y(B[2]), .Cin(volladdierer_2_cout), .Cout(volladdierer_3_cout), .S(S[2]));
  Volladdierer volladdierer_4 (.x(A[3]), .y(B[3]), .Cin(volladdierer_3_cout), .Cout(volladdierer_4_cout), .S(S[3]));
  Volladdierer volladdierer_5 (.x(A[4]), .y(B[4]), .Cin(volladdierer_4_cout), .Cout(volladdierer_5_cout), .S(S[4]));
  Volladdierer volladdierer_6 (.x(A[5]), .y(B[5]), .Cin(volladdierer_5_cout), .Cout(volladdierer_6_cout), .S(S[5]));
  Volladdierer volladdierer_7 (.x(A[6]), .y(B[6]), .Cin(volladdierer_6_cout), .Cout(volladdierer_7_cout), .S(S[6]));
  Volladdierer volladdierer_8 (.x(A[7]), .y(B[7]), .Cin(volladdierer_7_cout), .Cout(Cout), .S(S[7]));
endmodule
