// Logisim project Logik.circ as structural Verilog: 1 circuit, main circuit main
module main (
  input  S1,
  input  S1_2,
  input  S2,
  input  S2_2,
  input  S1_3,
  input  S1_4,
  input  S1_5,
  input  S2_3,
  input  S2_4,
  input  S2_5,
  input  S1_6
);

  wire and_1_out, nand_1_out, nor_1_out, not_1_out, or_1_out, xor_1_out;

  and and_1 (and_1_out, S1, S2);
  or or_1 (or_1_out, S1_3, S2_3);
  not not_1 (not_1_out, S1_6);
  LED led_1 (.in(and_1_out));
  LED led_2 (.in(or_1_out));
  LED led_3 (.in(not_1_out));
  nand nand_1 (nand_1_out, S1_2, S2_2);
  LED led_4 (.in(nand_1_out));
  nor nor_1 (nor_1_out, S1_4, S2_4);
  LED led_5 (.in(nor_1_out));
  xor xor_1 (xor_1_out, S1_5, S2_5);
  LED led_6 (.in(xor_1_out));

  // Notes on the sheet:
  //   AND Schaltung
  //   OR Schaltung
  //   NOT Schaltung
  //   NAND Schaltung
  //   NOR Schaltung
  //   XOR Schaltung
endmodule
